# Fritzing sketch Circuito (saved by Fritzing 0.9.2b)
breadboards: 1

parts:
  M2 = ESC
  920KV_Motor2 = DJI 920 KV Motor
  Part2 = Arduino Uno (Rev3)
  Parte1 = AltIMU-10
  Power_plug1 = Power plug  # not connected
  R1 = Resistor [tolerance=±5% resistance=4.7k package=THT]
  LED1 = LED - 5mm [color="Green (560nm)" package="5 mm [THT]"]

nets:
  N1: M2.U, 920KV_Motor2.u
  N2: M2.V, 920KV_Motor2.v
  N3: M2.W, 920KV_Motor2.w
  N4: M2.DATA, Part2.D9_PWM
  GND: M2.GND, Part2.GND
  N5: Part2.A4/SDA, Parte1.SDA
  N6: Part2.A5/SCL, Parte1.SCL
  5V: Part2.5V, Parte1.VCC
  N7: R1.Pin_1, LED1.anode

custom parts:
  DJI 920 KV Motor: DJI Brushless Outrunner 2212/920K Motor F330-550
  AltIMU-10: Description: This is an AltIMU-10 v3 low-power three-axis angular rate sensor.
